// Logisim project codificador.circ as structural Verilog: 1 circuit, main circuit main
module main (
  input  g,
  input  f,
  input  e,
  input  d,
  input  c,
  input  b,
  input  a,
  output x,
  output y,
  output z
);

  wire and_1_out, and_2_out, and_3_out, and_4_out, not_2_out, not_3_out, not_4_out, not_5_out, or_2_out,
       or_3_out;

  not not_1 (x, d);
  not not_2 (not_2_out, d);
  not not_3 (not_3_out, b);
  not not_4 (not_4_out, d);
  not not_5 (not_5_out, f);
  and and_1 (and_1_out, not_2_out, b);
  and and_2 (and_2_out, not_3_out, a);
  and and_3 (and_3_out, not_4_out, c);
  and and_4 (and_4_out, not_5_out, e);
  or or_1 (y, and_1_out, f);
  or or_2 (or_2_out, and_2_out, and_3_out);
  or or_3 (or_3_out, and_4_out, g);
  or or_4 (z, or_2_out, or_3_out);
endmodule
