// Logisim project decodificador.circ as structural Verilog: 1 circuit, main circuit main
module main (
  input  a,
  input  b,
  input  c,
  output x,
  output y,
  output z,
  output u,
  output v,
  output w,
  output s,
  output t
);

  wire not_1_out, not_2_out, not_3_out, not_4_out, not_5_out, not_6_out, not_7_out, not_8_out, not_9_out,
       not_10_out, not_11_out, not_12_out;

  not not_1 (not_1_out, a);
  not not_2 (not_2_out, a);
  not not_3 (not_3_out, c);
  not not_4 (not_4_out, a);
  not not_5 (not_5_out, b);
  not not_6 (not_6_out, a);
  not not_7 (not_7_out, b);
  not not_8 (not_8_out, c);
  not not_9 (not_9_out, c);
  not not_10 (not_10_out, b);
  not not_11 (not_11_out, b);
  not not_12 (not_12_out, c);
  and and_1 (x, not_1_out, b, c);
  and and_2 (y, not_2_out, b, not_3_out);
  and and_3 (z, not_4_out, not_5_out, c);
  and and_4 (u, not_6_out, not_7_out, not_8_out);
  and and_5 (v, a, b, c);
  and and_6 (w, a, b, not_9_out);
  and and_7 (s, a, not_10_out, c);
  and and_8 (t, a, not_11_out, not_12_out);
endmodule
